# Fritzing sketch led-pumpkin (saved by Fritzing 0.9.4)
circuit board: 2.70854cm x 4.58128cm
breadboards: 1

parts:
  Part1 = ws2812b [package="smd 2812b"]
  R1 = Resistor [tolerance=±5% resistance=470 package=THT]
  WeMos_D1_Mini1 = WeMos D1 Mini
  C1 = Electrolytic Capacitor [capacitance=1mF package="100 mil [THT, electrolytic]"]
  D1 = Diode [package=diode-1n4148]
  J3 = Dagu DGServo 9g header (male) [package=THT]
  J2 = screw terminal, 2 pins

nets:
  N1: Part1.VDD, D1.C
  N2: Part1.DOUT, J3.Vcc
  GND: Part1.VSS, WeMos_D1_Mini1.G, C1.-, J3.gnd, J2.pin1
  N3: Part1.DIN, R1.Pin_0
  N4: R1.Pin_1, WeMos_D1_Mini1.D1
  N5: WeMos_D1_Mini1.5V, C1.+, D1.A, J3.pulse, J2.pin2
